# Fritzing sketch Sketch (saved by Fritzing 0.9.3b)
breadboards: 1

parts:
  WeMos_D1_Mini1 = WeMos D1 Mini
  Q1 = MOSFET-NCHANNEL [part_number=IRF540 package=to220v]
  LED1 = LED - 5mm [color="Red (633nm)" package="5 mm [THT]"]
  J1 = Basic Servo
  J2 = Basic Servo

nets:
  VCC: WeMos_D1_Mini1.5V, LED1.cathode, J1.vcc, J2.vcc
  N1: WeMos_D1_Mini1.D3, J1.pulse
  N2: WeMos_D1_Mini1.D5, Q1.G
  N3: WeMos_D1_Mini1.D7, J2.pulse
  GND: WeMos_D1_Mini1.G, Q1.S, J1.gnd, J2.gnd
  N4: Q1.D, LED1.anode

notes:
  yAxis servo : D7
  xAxis servo : D3
  IRF540 : D5
  Laser
